// Logisim project CPU_but_how_do_it_know.circ as structural Verilog: 16 circuits, main circuit main
module main (
  input  [7:0] in_1,
  input  in_2,
  input  in_3,
  input  in_4,
  input  in_5,
  input  in_6,
  output out_7,
  output [7:0] out_8
);

  rightshifters rightshifters_1 (
    .in_1(in_1), .in_3(in_3), .in_4(in_4), .in_2(in_2), .in_5(in_5), .in_6(in_6), .out_7(out_7), .out_8(out_8));
endmodule

module memorybit (
  input  in_1,
  input  in_2,
  output out_3
);

  wire nand_1_out, nand_2_out, nand_4_out;

  nand nand_1 (nand_1_out, in_1, in_2);
  nand nand_2 (nand_2_out, nand_1_out, in_2);
  nand nand_3 (out_3, nand_1_out, nand_4_out);
  nand nand_4 (nand_4_out, out_3, nand_2_out);
endmodule

module \byte  (
  input  in_1,
  input  in_2,
  input  in_3,
  input  in_4,
  input  in_5,
  input  in_6,
  input  in_7,
  input  in_8,
  input  in_9,
  output out_10,
  output out_11,
  output out_12,
  output out_13,
  output out_14,
  output out_15,
  output out_16,
  output out_17
);

  memorybit memorybit_1 (.in_2(in_9), .in_1(in_1), .out_3(out_10));
  memorybit memorybit_2 (.in_2(in_9), .in_1(in_2), .out_3(out_11));
  memorybit memorybit_3 (.in_2(in_9), .in_1(in_3), .out_3(out_12));
  memorybit memorybit_4 (.in_2(in_9), .in_1(in_4), .out_3(out_13));
  memorybit memorybit_5 (.in_2(in_9), .in_1(in_5), .out_3(out_14));
  memorybit memorybit_6 (.in_2(in_9), .in_1(in_6), .out_3(out_15));
  memorybit memorybit_7 (.in_2(in_9), .in_1(in_7), .out_3(out_16));
  memorybit memorybit_8 (.in_2(in_9), .in_1(in_8), .out_3(out_17));
endmodule

module enabler (
  input  in_1,
  input  in_2,
  input  in_3,
  input  in_4,
  input  in_5,
  input  in_6,
  input  in_7,
  input  in_8,
  input  in_9,
  output out_10,
  output out_11,
  output out_12,
  output out_13,
  output out_14,
  output out_15,
  output out_16,
  output out_17
);

  assign out_10 = in_9 ? in_1 : 1'bz;  // Controlled_Buffer controlled_buffer_1
  assign out_11 = in_9 ? in_2 : 1'bz;  // Controlled_Buffer controlled_buffer_2
  assign out_12 = in_9 ? in_3 : 1'bz;  // Controlled_Buffer controlled_buffer_3
  assign out_13 = in_9 ? in_4 : 1'bz;  // Controlled_Buffer controlled_buffer_4
  assign out_14 = in_9 ? in_5 : 1'bz;  // Controlled_Buffer controlled_buffer_5
  assign out_15 = in_9 ? in_6 : 1'bz;  // Controlled_Buffer controlled_buffer_6
  assign out_16 = in_9 ? in_7 : 1'bz;  // Controlled_Buffer controlled_buffer_7
  assign out_17 = in_9 ? in_8 : 1'bz;  // Controlled_Buffer controlled_buffer_8
endmodule

module registerBE (
  input  in_1,
  input  in_2,
  input  in_3,
  input  in_4,
  input  in_5,
  input  in_6,
  input  in_7,
  input  in_8,
  input  in_9,
  input  in_10,
  output out_11,
  output out_12,
  output out_13,
  output out_14,
  output out_15,
  output out_16,
  output out_17,
  output out_18
);

  wire byte_1_out_10, byte_1_out_11, byte_1_out_12, byte_1_out_13, byte_1_out_14, byte_1_out_15,
       byte_1_out_16, byte_1_out_17;

  \byte  byte_1 (
    .in_3(in_3), .in_4(in_4), .in_5(in_5), .in_6(in_6), .in_7(in_7), .in_8(in_8), .in_1(in_1), .in_2(in_2),
    .in_9(in_9), .out_12(byte_1_out_12), .out_13(byte_1_out_13), .out_14(byte_1_out_14),
    .out_15(byte_1_out_15), .out_16(byte_1_out_16), .out_17(byte_1_out_17), .out_10(byte_1_out_10),
    .out_11(byte_1_out_11));
  enabler enabler_1 (
    .in_1(byte_1_out_10), .in_2(byte_1_out_11), .in_3(byte_1_out_12), .in_4(byte_1_out_13),
    .in_5(byte_1_out_14), .in_6(byte_1_out_15), .in_7(byte_1_out_16), .in_8(byte_1_out_17), .in_9(in_10),
    .out_10(out_11), .out_11(out_12), .out_12(out_13), .out_13(out_14), .out_14(out_15), .out_15(out_16),
    .out_16(out_17), .out_17(out_18));
endmodule

module magicbus (
  input  [7:0] in_1,
  input  in_2,
  input  in_3,
  input  in_4,
  input  in_5,
  input  in_6,
  input  in_7,
  input  in_8,
  input  in_9,
  input  in_10,
  input  in_11,
  output [7:0] out_12
);

  registerBEsimple registerbesimple_1 (.in_1(in_1), .in_2(in_2), .in_3(in_3), .out_4(out_12));
  registerBEsimple registerbesimple_2 (.in_1(out_12), .in_2(in_4), .in_3(in_5), .out_4(out_12));
  registerBEsimple registerbesimple_3 (.in_1(out_12), .in_2(in_6), .in_3(in_7), .out_4(out_12));
  registerBEsimple registerbesimple_4 (.in_1(out_12), .in_2(in_8), .in_3(in_9), .out_4(out_12));
  registerBEsimple registerbesimple_5 (.in_1(out_12), .in_2(in_10), .in_3(in_11), .out_4(out_12));
endmodule

module registerBEsimple (
  input  [7:0] in_1,
  input  in_2,
  input  in_3,
  output [7:0] out_4
);

  registerBE registerbe_1 (
    .in_9(in_2), .in_10(in_3), .in_1(in_1[0]), .in_2(in_1[1]), .in_3(in_1[2]), .in_4(in_1[3]),
    .in_5(in_1[4]), .in_6(in_1[5]), .in_7(in_1[6]), .in_8(in_1[7]), .out_11(out_4[0]), .out_12(out_4[1]),
    .out_13(out_4[2]), .out_14(out_4[3]), .out_15(out_4[4]), .out_16(out_4[5]), .out_17(out_4[6]),
    .out_18(out_4[7]));
endmodule

module RAM256Cell (
  input  in_1,
  input  [7:0] in_2,
  input  in_3,
  input  in_4,
  input  in_5,
  output [7:0] out_6
);

  wire and_1_out, and_2_out, and_3_out;

  and and_1 (and_1_out, in_1, in_3);
  and and_2 (and_2_out, and_1_out, in_4);
  and and_3 (and_3_out, and_1_out, in_5);
  registerBEsimple registerbesimple_1 (.in_1(in_2), .in_2(and_2_out), .in_3(and_3_out), .out_4(out_6));
endmodule

module MUX2to1 (
  input  in_1,
  input  in_2,
  input  in_3,
  output out_4
);

  wire and_1_out, and_2_out, not_1_out;

  and and_1 (and_1_out, in_1, in_3);
  and and_2 (and_2_out, in_2, not_1_out);
  not not_1 (not_1_out, in_3);
  or or_1 (out_4, and_1_out, and_2_out);
endmodule

module MUX8bit2to1 (
  input  [7:0] in_1,
  input  [7:0] in_2,
  input  in_3,
  output [7:0] out_4
);

  MUX2to1 mux2to1_1 (.in_1(in_1[0]), .in_2(in_2[0]), .in_3(in_3), .out_4(out_4[0]));
  MUX2to1 mux2to1_2 (.in_1(in_1[1]), .in_2(in_2[1]), .in_3(in_3), .out_4(out_4[1]));
  MUX2to1 mux2to1_3 (.in_1(in_1[2]), .in_2(in_2[2]), .in_3(in_3), .out_4(out_4[2]));
  MUX2to1 mux2to1_4 (.in_1(in_1[3]), .in_2(in_2[3]), .in_3(in_3), .out_4(out_4[3]));
  MUX2to1 mux2to1_5 (.in_1(in_1[4]), .in_2(in_2[4]), .in_3(in_3), .out_4(out_4[4]));
  MUX2to1 mux2to1_6 (.in_1(in_1[5]), .in_2(in_2[5]), .in_3(in_3), .out_4(out_4[5]));
  MUX2to1 mux2to1_7 (.in_1(in_1[6]), .in_2(in_2[6]), .in_3(in_3), .out_4(out_4[6]));
  MUX2to1 mux2to1_8 (.in_1(in_1[7]), .in_2(in_2[7]), .in_3(in_3), .out_4(out_4[7]));
endmodule

module RAM4times4 (
  input  in_1,
  input  in_2,
  input  in_3,
  input  in_4,
  input  in_5,
  input  in_6,
  input  in_7,
  input  in_8,
  input  in_9,
  input  in_10,
  input  in_11,
  input  in_12,
  input  in_13,
  input  [7:0] in_14,
  input  in_15,
  input  in_16,
  input  in_17,
  output [7:0] out_18,
  output [7:0] out_19,
  output [7:0] out_20,
  output out_21
);

  wire [7:0] adder8bit_1_out_5, controlled_buffer_1_out, mux8bit2to1_1_out_4;

  RAM256Cell ram256cell_1 (.in_1(in_3), .in_3(in_1), .in_4(in_10), .in_5(in_11), .in_2(out_19), .out_6(out_19));
  RAM256Cell ram256cell_2 (.in_1(in_6), .in_3(in_1), .in_4(in_10), .in_5(in_11), .in_2(out_19), .out_6(out_19));
  RAM256Cell ram256cell_3 (.in_1(in_3), .in_3(in_2), .in_4(in_10), .in_5(in_11), .in_2(out_19), .out_6(out_19));
  RAM256Cell ram256cell_4 (.in_1(in_6), .in_3(in_2), .in_4(in_10), .in_5(in_11), .in_2(out_19), .out_6(out_19));
  assign controlled_buffer_1_out = in_12 ? mux8bit2to1_1_out_4 : 8'bz;  // Controlled_Buffer controlled_buffer_1
  MUX8bit2to1 mux8bit2to1_1 (.in_3(in_17), .in_1(out_19), .in_2(in_14), .out_4(mux8bit2to1_1_out_4));
  registerBEsimple registerbesimple_1 (.in_1(controlled_buffer_1_out), .in_2(in_12), .in_3(in_13), .out_4(out_19));
  registerBEsimple registerbesimple_2 (.in_1(out_19), .in_2(in_4), .in_3(in_5), .out_4(out_18));
  registerBEsimple registerbesimple_3 (.in_1(out_19), .in_2(in_7), .in_3(in_8), .out_4(out_20));
  registerBEsimple registerbesimple_4 (.in_1(adder8bit_1_out_5), .in_2(in_15), .in_3(in_16), .out_4(out_19));
  adder8bit adder8bit_1 (.in_2(in_9), .in_3(out_20), .in_1(out_18), .out_4(out_21), .out_5(adder8bit_1_out_5));
endmodule

module adderbit1 (
  input  in_1,
  input  in_2,
  output out_3,
  output out_4
);

  xor xor_1 (out_3, in_1, in_2);
  and and_1 (out_4, in_1, in_2);
endmodule

module adder3bit1 (
  input  in_1,
  input  in_2,
  input  in_3,
  output out_4,
  output out_5
);

  wire adderbit1_1_out_3, adderbit1_1_out_4, adderbit1_2_out_4;

  adderbit1 adderbit1_1 (.in_1(in_2), .in_2(in_3), .out_3(adderbit1_1_out_3), .out_4(adderbit1_1_out_4));
  adderbit1 adderbit1_2 (.in_1(in_1), .in_2(adderbit1_1_out_3), .out_3(out_4), .out_4(adderbit1_2_out_4));
  or or_1 (out_5, adderbit1_2_out_4, adderbit1_1_out_4);
endmodule

module adder8bit (
  input  [7:0] in_1,
  input  in_2,
  input  [7:0] in_3,
  output out_4,
  output [7:0] out_5
);

  wire adder3bit1_2_out_5, adder3bit1_3_out_5, adder3bit1_4_out_5, adder3bit1_5_out_5, adder3bit1_6_out_5,
       adder3bit1_7_out_5, adder3bit1_8_out_5;

  adder3bit1 adder3bit1_1 (.in_2(in_1[7]), .in_3(in_3[7]), .in_1(adder3bit1_2_out_5), .out_4(out_5[7]), .out_5(out_4));
  adder3bit1 adder3bit1_2 (
    .in_2(in_1[6]), .in_3(in_3[6]), .in_1(adder3bit1_3_out_5), .out_4(out_5[6]), .out_5(adder3bit1_2_out_5));
  adder3bit1 adder3bit1_3 (
    .in_2(in_1[5]), .in_3(in_3[5]), .in_1(adder3bit1_4_out_5), .out_4(out_5[5]), .out_5(adder3bit1_3_out_5));
  adder3bit1 adder3bit1_4 (
    .in_2(in_1[4]), .in_3(in_3[4]), .in_1(adder3bit1_5_out_5), .out_4(out_5[4]), .out_5(adder3bit1_4_out_5));
  adder3bit1 adder3bit1_5 (
    .in_2(in_1[3]), .in_3(in_3[3]), .in_1(adder3bit1_6_out_5), .out_4(out_5[3]), .out_5(adder3bit1_5_out_5));
  adder3bit1 adder3bit1_6 (
    .in_2(in_1[2]), .in_3(in_3[2]), .in_1(adder3bit1_7_out_5), .out_4(out_5[2]), .out_5(adder3bit1_6_out_5));
  adder3bit1 adder3bit1_7 (
    .in_2(in_1[1]), .in_3(in_3[1]), .in_1(adder3bit1_8_out_5), .out_4(out_5[1]), .out_5(adder3bit1_7_out_5));
  adder3bit1 adder3bit1_8 (.in_2(in_1[0]), .in_3(in_3[0]), .in_1(in_2), .out_4(out_5[0]), .out_5(adder3bit1_8_out_5));
endmodule

module leftshifters (
  input  in_1,
  input  [7:0] in_2,
  input  in_3,
  input  in_4,
  input  in_5,
  input  in_6,
  output [7:0] out_7,
  output out_8
);

  wire registerbe_1_out_11, registerbe_1_out_12, registerbe_1_out_13, registerbe_1_out_14,
       registerbe_1_out_15, registerbe_1_out_16, registerbe_1_out_17;

  registerBE registerbe_1 (
    .in_9(in_3), .in_10(in_4), .in_1(in_2[0]), .in_2(in_2[1]), .in_3(in_2[2]), .in_4(in_2[3]),
    .in_5(in_2[4]), .in_6(in_2[5]), .in_7(in_2[6]), .in_8(in_2[7]), .out_11(registerbe_1_out_11),
    .out_12(registerbe_1_out_12), .out_13(registerbe_1_out_13), .out_14(registerbe_1_out_14),
    .out_15(registerbe_1_out_15), .out_16(registerbe_1_out_16), .out_17(registerbe_1_out_17), .out_18(out_8));
  registerBE registerbe_2 (
    .in_9(in_5), .in_10(in_6), .in_1(in_1), .in_2(registerbe_1_out_11), .in_3(registerbe_1_out_12),
    .in_4(registerbe_1_out_13), .in_5(registerbe_1_out_14), .in_6(registerbe_1_out_15),
    .in_7(registerbe_1_out_16), .in_8(registerbe_1_out_17), .out_11(out_7[0]), .out_12(out_7[1]),
    .out_13(out_7[2]), .out_14(out_7[3]), .out_15(out_7[4]), .out_16(out_7[5]), .out_17(out_7[6]),
    .out_18(out_7[7]));
endmodule

module rightshifters (
  input  [7:0] in_1,
  input  in_2,
  input  in_3,
  input  in_4,
  input  in_5,
  input  in_6,
  output out_7,
  output [7:0] out_8
);

  wire registerbe_1_out_12, registerbe_1_out_13, registerbe_1_out_14, registerbe_1_out_15,
       registerbe_1_out_16, registerbe_1_out_17, registerbe_1_out_18;

  registerBE registerbe_1 (
    .in_9(in_3), .in_10(in_4), .in_1(in_1[0]), .in_2(in_1[1]), .in_3(in_1[2]), .in_4(in_1[3]),
    .in_5(in_1[4]), .in_6(in_1[5]), .in_7(in_1[6]), .in_8(in_1[7]), .out_11(out_7),
    .out_12(registerbe_1_out_12), .out_13(registerbe_1_out_13), .out_14(registerbe_1_out_14),
    .out_15(registerbe_1_out_15), .out_16(registerbe_1_out_16), .out_17(registerbe_1_out_17),
    .out_18(registerbe_1_out_18));
  registerBE registerbe_2 (
    .in_9(in_5), .in_10(in_6), .in_1(registerbe_1_out_12), .in_2(registerbe_1_out_13),
    .in_3(registerbe_1_out_14), .in_4(registerbe_1_out_15), .in_5(registerbe_1_out_16),
    .in_6(registerbe_1_out_17), .in_7(registerbe_1_out_18), .in_8(in_2), .out_11(out_8[0]),
    .out_12(out_8[1]), .out_13(out_8[2]), .out_14(out_8[3]), .out_15(out_8[4]), .out_16(out_8[5]),
    .out_17(out_8[6]), .out_18(out_8[7]));
endmodule
